# Fritzing sketch uber_bb01 (saved by Fritzing 0.9.3b)
circuit board: 2.8cm x 6cm
breadboards: 1

parts:
  Q1 = Basic FET N-Channel [package="TO220 [THT]"]
  Q3 = Basic FET N-Channel [package="TO220 [THT]"]
  JP1 = Header 4 [package=molex-1x4_lock]
  Q2 = Basic FET N-Channel [package="TO220 [THT]"]
  U1 = Adafruit Trinket 5V
  C2 = Electrolytic Capacitor [capacitance=1mF package="200 mil [THT, electrolytic]"]
  BATT1 = 3xAAA Switchable Battery Pack w/Bare Wire

nets:
  N1: Q1.gate, U1.#0
  N2: Q1.drain, JP1.4
  N3: Q1.source, Q3.source, Q2.source, U1.GND, C2.+, BATT1.NEG
  N4: Q3.gate, U1.#2
  N5: Q3.drain, JP1.2
  N6: JP1.3, Q2.drain
  N7: Q2.gate, U1.#1
  N8: U1.VBAT, C2.-, BATT1.POS

custom parts:
  Adafruit Trinket 5V: Trinket may be small, but do not be fooled by its size! It's a tiny microcontroller board, built around the Atmel ATtiny85, a little chip with a lot of power. We wanted to design a microcontroller board that was small enough to fit into any project, and low cost enough to use without hesitation. Perfect for when you don't want to give up your expensive dev-board and you aren't willing to take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
  3xAAA Switchable Battery Pack w/Bare Wire: 3xAAA Switchable Battery Pack w/Bare Wire Connectors
